# Fritzing sketch LcdPanel (saved by Fritzing 0.9.2b)
circuit board: 8.46667cm x 5.64444cm
breadboards: 1

parts:
  LCD1 = LCD screen
  R1 = Trimmer Potentiometer [maximum_resistance=10kΩ package=THT]
  Part1 = Arduino Uno (Rev3)

nets:
  VSS: LCD1.VSS, R1.leg1, Part1.GND
  VDD: LCD1.VDD, R1.leg2, Part1.5V
  N1: LCD1.V0, R1.wiper
  N2: LCD1.RS, Part1.D10_PWM/SS
  N3: LCD1.R/W, Part1.D11_PWM/MOSI
  N4: LCD1.E, Part1.D12/MISO
  N5: LCD1.DB0, Part1.D2
  N6: LCD1.DB1, Part1.D3_PWM
  N7: LCD1.DB2, Part1.D4
  N8: LCD1.DB3, Part1.D5_PWM
  N9: LCD1.DB4, Part1.D6_PWM
  N10: LCD1.DB5, Part1.D7
  N11: LCD1.DB6, Part1.D8
  N12: LCD1.DB7, Part1.D9_PWM

notes:
  Подключение LCD
  дисплея
